// Logisim project MIPS_ALU_CIRCUIT.circ as structural Verilog: 1 circuit, main circuit main
module main (
  input  [31:0] in_1,
  input  [31:0] in_2,
  input  [3:0] in_3,
  input  [4:0] in_4,
  output [31:0] out_5
);

  // Mips_ALU mips_alu_1: pin names not known; wires that end beside it: in_1, in_2, in_3, in_4, out_5
endmodule
